# Fritzing sketch arduino final project (saved by Fritzing 0.9.3b)
breadboards: 1

parts:
  Parça1 = Arduino Uno (Rev3)
  LED1 = smd LED [color="Red (633nm)" package="0603 [SMD]"]  # not connected
  U1 = POT [package=pot_alpha_rv16af-20]
  S1 = Pushbutton [package="[THT]"]
  J1 = Piezo Speaker
  LED2 = smd LED [color="Red (633nm)" package="0603 [SMD]"]
  LED3 = smd LED [color="Red (633nm)" package="0603 [SMD]"]
  LCD1 = LCD screen
  R1 = Photocell (LDR) [package=THT]
  R2 = Resistor [tolerance=±5% resistance=220 package="1206 [SMD]"]
  R3 = Resistor [tolerance=±5% resistance=220 package="1206 [SMD]"]
  R4 = Resistor [tolerance=±5% resistance=220 package="1206 [SMD]"]
  R5 = Resistor [tolerance=±5% resistance=220 package="1206 [SMD]"]
  R6 = Resistor [tolerance=±5% resistance=220 package="1206 [SMD]"]
  J2 = Basic Servo

nets:
  N1: Parça1.A0, R1.pin_0, R4.Pin_0
  N2: Parça1.A1, U1.S
  N3: Parça1.D8, LCD1.DB7
  N4: Parça1.D9_PWM, LCD1.DB6
  N5: Parça1.D10_PWM/SS, LCD1.DB5
  N6: Parça1.D11_PWM/MOSI, LCD1.DB4
  N7: Parça1.D12/MISO, J1.pin2
  N8: Parça1.D13/SCK, R2.Pin_1
  GND: Parça1.GND, U1.E, J1.pin1, LED2.cathode, LED3.cathode, LCD1.VSS, LCD1.V0, LCD1.R/W, LCD1.LED-, R3.Pin_0, R4.Pin_1, R6.Pin_0, J2.gnd
  N9: Parça1.D2, S1.Pin_1, S1.Pin_2, R3.Pin_1
  N10: Parça1.D3_PWM, R5.Pin_1
  N11: Parça1.D4, LCD1.RS
  N12: Parça1.D5_PWM, LCD1.E
  N13: Parça1.D6_PWM, J2.pulse
  5V: Parça1.5V, S1.Pin_3, S1.Pin_4, J2.vcc
  N14: U1.A, LCD1.VDD, LCD1.LED+, R1.pin_1
  N15: LED3.anode, R5.Pin_0
